# Fritzing sketch not-kiwi-bot (saved by Fritzing 0.9.3b)
breadboards: 1

parts:
  Raspberry_Pi_1 = Raspberry Pi 3 [part_number=RPI-3-V1.2]
  GP-20U7 = GP-20U7
  PWM1 = PCA9685 16x12-bit PWM Breakout
  GY1 = MPU-6050 Board GY-521 [form="♀ (female)" package=THT]
  Part3 = Arduino Micro (Rev3)
  hc-sr1 = hc-sr04
  hc-sr2 = hc-sr04

nets:
  3V3: Raspberry_Pi_1.3v3, Raspberry_Pi_1.3V3, GP-20U7.VCC, PWM1.no_name_yet#505, GY1.pin1
  N1: Raspberry_Pi_1.GPIO2, PWM1.no_name_yet#504, GY1.pin4
  N2: Raspberry_Pi_1.GPIO3, PWM1.no_name_yet#503, GY1.pin3
  N3: Raspberry_Pi_1.GPIO4, GY1.pin8
  GND: Raspberry_Pi_1.GND, GP-20U7.GND, PWM1.no_name_yet#501, GY1.pin2
  N4: Raspberry_Pi_1.GPIO15, GP-20U7.TX
  N5: Part3.D2/SDA, hc-sr1.Trig
  N6: Part3.D3/SCL, hc-sr1.Echo
  N7: Part3.D9_PWM/A9, hc-sr2.Trig
  N8: Part3.D10_PWM/A10, hc-sr2.Echo
  GND_2: Part3.GND, hc-sr2.GND
  5V: Part3.5V, hc-sr2.VCC

custom parts:
  MPU-6050 Board GY-521: Acelerometro y Giroscopio MPU-6050 Board GY-521
